# Fritzing sketch Subarino (saved by Fritzing 0.9.3b)

parts:
  Часть1 = Arduino Uno (Rev3)  # not connected
  Часть2 = Bluetooth HC-05 Macho
  Часть3 = BH1750
  Часть4 = Relay
  Часть5 = Relay
  U1 = XBee
  Part2 = Arduino Wireless SD Shield
  Part3 = Arduino Nano (Rev3.0) (ICSP)
  U2 = XBee  # not connected
  Part4 = Arduino Can-Bus Shield  # not connected
  Part5 = Memoire 1.0 - SD card log shield  # not connected
  Part6 = Arduino Uno (Rev3) - ICSP  # not connected
  Part7 = Arduino Wireless SD Shield
  U3 = XBee

nets:
  N1: Часть2.TXD, Part2.D3
  N2: Часть2.RXD, Part2.D2
  VCC: Часть2.VCC, Part2.+5V
  GND: Часть2.GND, U1.GND, Part2.GND
  VCC_2: Часть3.VCC, Part3.3V3
  GND_2: Часть3.GND, Часть4.GND, Часть5.GND, Part3.GND, Part3.VIN
  N3: Часть3.SCL, Part3.A6, Part3.A5
  N4: Часть3.SDA, Part3.A4
  N5: Часть3.ADDR, Part3.A3
  N6: Часть4.SIGNAL, Part3.D7
  VCC_3: Часть4.VCC, Часть5.VCC, Part3.5V
  N7: Часть5.SIGNAL, Part3.D8
  VCC_4: U1.VCC, Part2.3.3V
  N8: U1.pin2, Part2.TX
  N9: U1.pin3, Part2.RX3
  N10: U1.pin4, Part2.N$43
  N11: U1.pin5, Part2.5
  N12: U1.pin6, Part2.RSSI
  N13: U1.pin7, Part2.7
  N14: U1.pin8, Part2.8
  N15: U1.pin9, Part2.9
  3.3V: Part7.3.3V, U3.VCC
  N16: Part7.TX, U3.pin2
  N17: Part7.RX3, U3.pin3
  N18: Part7.N$43, U3.pin4
  N19: Part7.5, U3.pin5
  N20: Part7.RSSI, U3.pin6
  N21: Part7.7, U3.pin7
  N22: Part7.8, U3.pin8
  N23: Part7.9, U3.pin9
  GND_3: Part7.GND, U3.GND

notes:
  +

custom parts:
  BH1750: Light Sensor
  Relay: The official support forum: support@iteadstudio.com
